# Fritzing sketch Safe (saved by Fritzing 0.9.3b)
breadboards: 1

parts:
  RC522_RFID_Scanner = IC, SIP package, 8 pins
  Fingerprint_Scanner = IC, SIP package, 4 pins
  HC-06_Bluetooth = Bluetooth HC-06 Macho
  HC-SR04_UltraSonic_Sensor = hc-sr04
  Servo_Motor = Basic Servo
  Arduino_Uno = Arduino Uno (Rev3) - ICSP
  R1 = Resistor [tolerance=±5% resistance=220 package="0402 [SMD]"]
  R2 = Resistor [tolerance=±5% resistance=220 package="0402 [SMD]"]
  R3 = Resistor [tolerance=±5% resistance=220 package="0402 [SMD]"]
  RGB_LED = RGB LED - (4 legs) [package="5 mm [THT]"]
  BAT1 = Battery Holders [package=battery-aa]
  BAT2 = Battery Holders [package=battery-aa]
  BAT3 = Battery Holders [package=battery-aa]
  6_Volts = Battery Holders [package=battery-aa]
  9_Volts = BC9VPC [package=bc9vpc]  # not connected

nets:
  N1: RC522_RFID_Scanner.pin1, Arduino_Uno.D10_PWM/SS
  N2: RC522_RFID_Scanner.pin2, Arduino_Uno.D13/SCK
  N3: RC522_RFID_Scanner.pin3, Arduino_Uno.D11_PWM/MOSI
  N4: RC522_RFID_Scanner.pin4, Arduino_Uno.D12/MISO
  GND: RC522_RFID_Scanner.pin6, Fingerprint_Scanner.pin1, HC-06_Bluetooth.GND, HC-SR04_UltraSonic_Sensor.GND, Servo_Motor.gnd, Arduino_Uno.GND, RGB_LED.common_anode, BAT1.+, BAT2.+, BAT3.+, 6_Volts.+
  N5: RC522_RFID_Scanner.pin7, Arduino_Uno.D9_PWM
  N6: RC522_RFID_Scanner.pin8, Arduino_Uno.3V3
  N7: Fingerprint_Scanner.pin2, Arduino_Uno.D3_PWM
  N8: Fingerprint_Scanner.pin3, Arduino_Uno.D2
  VCC: Fingerprint_Scanner.pin4, HC-06_Bluetooth.VCC, Arduino_Uno.5V
  N9: HC-06_Bluetooth.TXD, Arduino_Uno.D0/RX
  N10: HC-06_Bluetooth.RXD, Arduino_Uno.D1/TX
  VCC_2: HC-SR04_UltraSonic_Sensor.VCC, Servo_Motor.vcc, BAT1.-, BAT2.-, BAT3.-, 6_Volts.-
  N11: HC-SR04_UltraSonic_Sensor.Trig, Arduino_Uno.D4
  N12: HC-SR04_UltraSonic_Sensor.Echo, Arduino_Uno.D5_PWM
  N13: Servo_Motor.pulse, Arduino_Uno.D6_PWM
  N14: Arduino_Uno.A0, R2.Pin_0
  N15: Arduino_Uno.A1, R1.Pin_0
  N16: Arduino_Uno.A2, R3.Pin_0
